# Fritzing sketch fan_controller_v6 (saved by Fritzing 0.9.3b)
stripboards: 2
perfboards: 1

parts:
  DHT1 = DHT11 Humitidy and Temperature Sensor
  R1 = Resistor [tolerance=±5% resistance=10k package=THT]
  Composant2 = LCD1602-I2C
  FET1 = STP16NF06 N-Channel Power MOSFET
  VCC1 = Battery block 9V
  M1 = DC Motor  # not connected
  R2 = Resistor [tolerance=±5% resistance=220 package="0603 [SMD]"]
  R5 = Resistor [tolerance=±5% resistance=10k package="0402 [SMD]"]
  Composant3 = Arduino Nano (Rev3.0)
  U3 = mystery part, 3 pins [chip_label=?]
  J1 = Piezo Speaker
  R6 = Resistor [tolerance=±5% resistance=220 package=THT]
  C1 = Ceramic Capacitor [capacitance=220µF voltage=25V package="100 mil [THT, multilayer]"]  # not connected
  R7 = Resistor [tolerance=±5% resistance=100 package=THT]
  D1 = Rectifier Diode [part_number=1N4001 package="300 mil [THT]"]
  S1 = Pushbutton [package="[THT]"]
  S2 = Pushbutton [package="[THT]"]

nets:
  VDD: DHT1.VDD, R1.Pin_0, Composant2.VCC, Composant3.5V
  N1: DHT1.DATA, R1.Pin_1, Composant3.D7
  GND: DHT1.GND, Composant2.GND, FET1.gate, FET1.drain, FET1.source, VCC1.-, R2.Pin_0, R2.Pin_1, R5.Pin_0, R5.Pin_1, Composant3.GND, Composant3.D11/MOSI, R6.Pin_0, S2.Pin_2
  N2: Composant2.SDA, Composant3.A4
  N3: Composant2.SCL, Composant3.A5
  N4: VCC1.+, Composant3.VIN
  N5: Composant3.D2, S1.Pin_3, S1.Pin_4
  N6: Composant3.D3, S2.Pin_4
  N7: Composant3.D9, U3.pin2
  N8: Composant3.D10, U3.pin1
  N9: Composant3.D12/MISO, J1.pin2
  N10: R7.Pin_1, D1.cathode

notes:
  DHT11
  Temperature Range: 0-50 °C
  Operating Voltage: 3V to 5.5V
  I2C LCD
  A 10K Ohm pull-up resistor is needed between the signal line and 5V line to make sure the signal level stays high by default
  12V 2A from AC/DC adaptor
  The gate resitor ... https://www.baldengineer.com/7-mosfet-myths-and-misconceptions-addressed.html
  Virtual ...
  Timer1 use pin 9 &10
  8&5
  PWM is not good to control 3 pin fan.
  A 1N4004 diode + 100 Ohms resistor + 220uF capacitor hep to reduce noise at low speed. PWW is reduced at 31Hz on board
  UP & Down
  (use internal 20k pull-up resistor)

custom parts:
  DHT11 Humitidy and Temperature Sensor: DHT11 Humidity and Temperature Sensor
  LCD1602-I2C: A standard character display, usually with 2x16 characters. Comes in many colors with LCM1602 IIC attached.
  STP16NF06 N-Channel Power MOSFET: STP16NF06 N-channel Power MOSFET
